# Fritzing sketch breadboard (saved by Fritzing 0.9.4)
breadboards: 1

parts:
  Part1 = Adafruit Feather M0 WINC1500 [part_number="Adafruit #3010"]
  R2 = Resistor [tolerance=±5% resistance=220 package="0603 [SMD]"]
  R3 = Resistor [tolerance=±5% resistance=220 package="0603 [SMD]"]
  R4 = Resistor [tolerance=±5% resistance=220k package="0603 [SMD]"]
  R5 = Resistor [tolerance=±5% resistance=1M package="0603 [SMD]"]
  LED1 = RGB LED (com. anode, rbg) [package="5 mm [THT]"]
  R1 = Resistor [tolerance=±5% resistance=220 package="0603 [SMD]"]

nets:
  N1: Part1.A0, R4.Pin_1, R5.Pin_0
  N2: Part1.GND, R4.Pin_0, LED1.common_anode
  N3: Part1.D11, R3.Pin_1
  N4: Part1.D10, R2.Pin_1
  N5: Part1.D9, R1.Pin_1
  N6: R2.Pin_0, LED1.green_cathode
  N7: R3.Pin_0, LED1.blue_cathode
  N8: LED1.red_cathode, R1.Pin_0

notes:
  Battery being monitored

custom parts:
  Adafruit Feather M0 WINC1500: This is the Adafruit Feather M0 WiFi w/ATWINC1500 - our take on an 'all-in-one' Arduino-compatible + high speed, reliable WiFi with built in USB and battery charging. Its an Adafruit Feather M0 with a WiFi module, ready to rock! Connect your Feather to the Internet with this fine new FCC-certified WiFi module from Atmel. This 802.11bgn-capable WiFi module is the best new thing for networking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

// code stored in the sketch: battery-monitor-breadboard.ino

