# Fritzing sketch shield (saved by Fritzing 0.9.4)
perfboards: 1

parts:
  Part1 = Adafruit FeatherWing Proto [part_number="Adafruit #2884"]
  J1 = Screw terminal - 2 pins [package=THT]  # not connected
  J2 = Screw terminal - 2 pins [package=THT]  # not connected
  R1 = Resistor [tolerance=±5% resistance=220 package="0603 [SMD]"]
  R2 = Resistor [tolerance=±5% resistance=220 package="0603 [SMD]"]
  R3 = Resistor [tolerance=±5% resistance=220 package="0603 [SMD]"]
  LED2 = RGB LED (com. anode, rbg) [package="5 mm [THT]"]
  R4 = Resistor [tolerance=±5% resistance=1M package="0603 [SMD]"]
  R5 = Resistor [tolerance=±5% resistance=220k package="0603 [SMD]"]

nets:
  N1: Part1.L, Part1.N$111, R3.Pin_0
  N2: Part1.K, Part1.N$110, R2.Pin_0
  N3: Part1.J, Part1.N$109, R1.Pin_0
  N4: Part1.A, Part1.N$87, R4.Pin_1, R5.Pin_1
  N5: Part1.GND, Part1.N$38, Part1.N$47, Part1.N$129, LED2.common_anode, R5.Pin_0
  N6: Part1.N$44, Part1.N$68, R4.Pin_0
  N7: Part1.N$125, R1.Pin_1, LED2.red_cathode
  N8: Part1.N$126, R2.Pin_1, LED2.green_cathode
  N9: Part1.N$127, R3.Pin_1, LED2.blue_cathode

custom parts:
  Adafruit FeatherWing Proto: This is the FeatherWing Proto - a prototyping add-on for all Feather boards. Using our Feather Stacking Headers or Feather Female Headers you can connect a FeatherWing on top or bottom of your Feather board and let the board take flight! This has a duplicate breakout for each pin on a Feather, as well as a bunch of plain grid proto holes. For GND and 3.3V, we give you a strip of connected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
